# Fritzing sketch Wiring Diagram (saved by Fritzing 0.9.3b)
breadboards: 1

parts:
  HC-SR04_Sensor_1 = HC-SR04 Ultrasonic Distance Sensor
  U1 = ESP32S-HiLetgo [part_number=ESP32S-HiLetgo]
  e-radionica1 = TCS230 Color Sensor [part_number=101209]
  LCM1602_IIC1 = LCM1602 IIC [part_number="LCM1602 IIC" chip_label="LCM1602 IIC" package="DIP (Dual Inline) [THT]"]
  U2 = LCD-16X2 [package=lcd-16x2]

nets:
  VCC: HC-SR04_Sensor_1.VCC, e-radionica1.Vcc, LCM1602_IIC1.VCC
  N1: HC-SR04_Sensor_1.TRIG, U1.GPIO35
  N2: HC-SR04_Sensor_1.ECHO, U1.GPIO32
  GND: HC-SR04_Sensor_1.GND, e-radionica1.Gnd, LCM1602_IIC1.GND
  N3: U1.GPIO25, e-radionica1.S3
  N4: U1.GPIO26, e-radionica1.S2
  N5: U1.GPIO27, e-radionica1.Out
  N6: U1.GPIO14, e-radionica1.S0
  N7: U1.GPIO12, e-radionica1.S1
  N8: U1.GPIO13, e-radionica1.OE
  N9: U1.GPIO21, LCM1602_IIC1.SDA
  N10: U1.GPIO22, LCM1602_IIC1.SCL
  VSS: LCM1602_IIC1.VSS, U2.VSS
  VDD: LCM1602_IIC1.VDD, U2.VDD
  N11: LCM1602_IIC1.V0, U2.VO
  N12: LCM1602_IIC1.RS, U2.RS
  N13: LCM1602_IIC1.RW, U2.R_W
  N14: LCM1602_IIC1.E, U2.E
  N15: LCM1602_IIC1.D0, U2.DB0
  N16: LCM1602_IIC1.D1, U2.DB1
  N17: LCM1602_IIC1.D2, U2.DB2
  N18: LCM1602_IIC1.D3, U2.DB3
  N19: LCM1602_IIC1.D4, U2.DB4
  N20: LCM1602_IIC1.D5, U2.DB5
  N21: LCM1602_IIC1.D6, U2.DB6
  N22: LCM1602_IIC1.D7, U2.DB7
  N23: LCM1602_IIC1.A, U2.A
  N24: LCM1602_IIC1.K, U2.K

custom parts:
  ESP32S-HiLetgo: HiLetgo ESP-WROOM-32 ESP32 ESP-32S Development Board 2.4GHz Dual-Mode WiFi + Bluetooth Dual Cores Microcontroller The ESP32 integrated with Antenna switches, RF Balun, power amplifiers, low-noise amplifiers, filters, and management modules, and the entire solution occupies the least area of PCB. 2.4 GHz Wi-Fi plus Bluetooth dual-mode chip, with TSMC Ultra-low power consumption 40nm technology,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
  TCS230 Color Sensor: TCS230
  LCM1602 IIC: I2C-Module to use a 1602 or 2004 LCD on with the wire.h libory Serial LCD Modul
